# Fritzing sketch Design_1 (saved by Fritzing 0.8.7b)
breadboards: 1

parts:
  Raspberry_Pi_Zero1 = Raspberry Pi Zero
  M1 = 5-ir-array-sensor [package=THT]
  BATT1 = LiPoly Battery (1300mAh)
  M2 = DC Motor
  M4 = DC Motor
  X1 = USB Connectors [package=usb-a-h]
  BATT2 = LiPoly Battery (1300mAh)
  S1 = SWITCH-MOMENTARY-2 [package=tactile-switch-1101ne]
  S2 = SWITCH-MOMENTARY-2 [package=tactile-switch-1101ne]
  M5 = L293D Motor Driver
  Part3 = PowerBoost 500 Charger
  Part4 = PowerBoost 500 Charger

nets:
  N1: Raspberry_Pi_Zero1.GIPO9, M1.VCC
  N2: Raspberry_Pi_Zero1.GIPO5, M1.S5
  N3: Raspberry_Pi_Zero1.GIPO6, M1.S4
  N4: Raspberry_Pi_Zero1.GIPO13, M1.S3
  N5: Raspberry_Pi_Zero1.GIPO19, M1.S2
  GND: Raspberry_Pi_Zero1.GIPO26, Raspberry_Pi_Zero1.GND, M1.S1, M1.GND, BATT1.negative, X1.GND, BATT2.negative, Part3.GND, Part4.GND
  N6: Raspberry_Pi_Zero1.5V, S1.1
  N7: BATT1.positive, Part4.VBAT
  N8: M2.pin_1, M2.pin_2, M4.pin_1, M4.pin_2, BATT2.positive, S2.2, M5.pin_9, M5.pin_10, M5.pin_11, M5.pin_12
  N9: X1.D+, S2.1
  N10: S1.2, Part4.5.0V
  N11: Part3.5.0V, Part4.USB

notes:
  converting 3v to 5v

custom parts:
  5-ir-array-sensor: 5 IR array sensor.
  LiPoly Battery (1300mAh): Lithium Ion Polymer Battery (1300mAh)
  PowerBoost 500 Charger: The PowerBoost 500C is a little DC/DC boost converter module that can be powered by any 3.7V LiIon/LiPoly battery, and convert the battery output to 5.2V DC for running your 5V projects. At its heart is a TPS61090 boost converter from TI. This boost converter chip has some really nice extras such as low battery detection, 2A internal switch, synchronous conversion, excellent efficiency, and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
