# Fritzing sketch Design_2 (saved by Fritzing 0.8.7b)
breadboards: 1

parts:
  M1 = 5-ir-array-sensor [package=THT]
  Part1 = Adafruit PowerBoost 1000C [part_number="Adafruit #2465"]
  M4 = DC Motor
  X1 = USB Connectors [package=usb-a-h]
  Mod1 = SparkFun_Auto_pHAT
  U2 = LIPO-2000mAh [package=lipo-2000]
  U3 = SPDT Slide Switch [package=ayz0202]
  U4 = SPDT Slide Switch [package=ayz0202]
  U5 = SPDT Slide Switch [package=ayz0202]
  U6 = SPDT Slide Switch [package=ayz0202]
  U7 = SPDT Slide Switch [package=ayz0202]
  M5 = DC Motor
  U8 = SPDT Slide Switch [package=ayz0202]
  U9 = LIPO-1000mAh [package=lipo-1000]

nets:
  N1: M1.S5, Mod1.GPIO26
  N2: M1.S4, Mod1.GPIO19
  N3: M1.S3, Mod1.GPIO13
  N4: M1.S2, Mod1.GPIO6
  GND: M1.S1, M1.GND, Part1.GND, X1.GND, Mod1.GND-6, Mod1.GPIO5, Mod1.GND-30, Mod1.GND-39, U9.-
  N5: M1.VCC, Mod1.GPIO9
  N6: Part1.VBUS, X1.D+, U8.3, U9.+
  N7: Part1.VLIPO, U2.+
  N8: Part1.ENABLE, U2.-
  N9: Part1.5.0V, U3.5
  N10: M4.pin_1, U6.5
  N11: M4.pin_2, U7.2
  N12: Mod1.AOUT1, U7.1
  N13: Mod1.AOUT2, U6.6
  N14: Mod1.BOUT1, U5.1
  N15: Mod1.BOUT2, U4.6
  N16: Mod1.MTR-PWR, Mod1.5V-IN, Mod1.5V-2, Mod1.5V-4, U3.6
  N17: U4.5, M5.pin_1
  N18: U4.4, U6.4, U8.2
  N19: U5.2, M5.pin_2

custom parts:
  5-ir-array-sensor: 5 IR array sensor.
  Adafruit PowerBoost 1000C: PowerBoost 1000C is the perfect power supply for your portable project! With a built-in load-sharing battery charger circuit, you'll be able to keep your power-hungry project running even while recharging the battery! This little DC/DC boost converter module can be powered by any 3.7V LiIon/LiPoly battery, and convert the battery output to 5.2V DC for running your 5V projects.
  SparkFun_Auto_pHAT: Sparkfun SparkFun_Auto_pHAT Raspberry PI hat.
